# Fritzing sketch speech_ex (saved by Fritzing 0.9.6b)
breadboards: 1

parts:
  J3 = shrouded pin header, 24 pins [form="♂ (shrouded male)"]
  LED1 = RGB LED (com. cathode, rgb) [package="5 mm [THT]"]
  R1 = Resistor [tolerance=±5% resistance=220 package="1206 [SMD]"]

nets:
  N1: J3.pin14, R1.Pin_0
  N2: J3.pin19, LED1.green_anode
  N3: J3.pin20, LED1.blue_anode
  N4: J3.pin24, LED1.red_anode
  N5: LED1.common_cathode, R1.Pin_1

notes:
  ESP32-S3-BOX3-BREAD
  GND -> Com. Cathode
  G13 -> RGB Red
  G12 -> RGB Green
  G11 -> RGB Blue
