# Fritzing sketch audio_ex_button_set (saved by Fritzing 0.9.6b)
breadboards: 1

parts:
  S1 = Pushbutton [package="[THT]"]
  S2 = Pushbutton [package="[THT]"]
  S3 = Pushbutton [package="[THT]"]
  JP1 = Header 6 [package=1x06-smd-female]
  R1 = Resistor [tolerance=±5% resistance=10k package="2512 [SMD]"]
  R2 = Resistor [tolerance=±5% resistance=10k package="2512 [SMD]"]
  R3 = Resistor [tolerance=±5% resistance=10k package="2512 [SMD]"]

nets:
  N1: S1.Pin_1, S1.Pin_2, JP1.6, R1.Pin_0
  N2: S1.Pin_3, S1.Pin_4, S2.Pin_3, S2.Pin_4, S3.Pin_3, S3.Pin_4, JP1.1
  N3: S2.Pin_1, S2.Pin_2, JP1.5, R2.Pin_0
  N4: S3.Pin_1, S3.Pin_2, JP1.4, R3.Pin_0
  N5: JP1.2, R1.Pin_1, R2.Pin_1, R3.Pin_1

notes:
  Gnd -> black
  3V3 -> red
  GPIO12 -> yellow
  GPIO11 -> Green
  GPIO14 -> Blue
