# Fritzing sketch led_button (saved by Fritzing 0.9.6b)
breadboards: 1

parts:
  LED1 = smd LED [color="Red (633nm)" package="0603 [SMD]"]
  R1 = Resistor [tolerance=±5% resistance=220 power=0.25 package=THT]
  S2 = Momentary Switch [package=ksa_sealed_tac_switch]
  J1 = shrouded pin header, 12 pins [form="♂ (shrouded male)"]

nets:
  N1: LED1.cathode, R1.Pin_1
  N2: LED1.anode, J1.pin2
  N3: R1.Pin_0, S2.1, J1.pin5
  N4: S2.4, J1.pin1

notes:
  Devkit/PMOD1
  Button -> IO38
  LED -> IO39
