# Fritzing sketch spi_ex (saved by Fritzing 0.9.6b)

parts:
  M1 = ESP32-C3-DevKitM-1 [part_number=ESP32-C3-DevKitM-1]
  microSD_Transflash1 = SparkFun - microSD Transflash
  R1 = Resistor [tolerance=±5% resistance=10k package="2512 [SMD]"]
  R2 = Resistor [tolerance=±5% resistance=10k package="2512 [SMD]"]
  R3 = Resistor [tolerance=±5% resistance=10k package="2512 [SMD]"]
  R4 = Resistor [tolerance=±5% resistance=10k package="2512 [SMD]"]

nets:
  N1: M1.4, microSD_Transflash1.DO, R1.Pin_0
  N2: M1.5, microSD_Transflash1.SCK, R2.Pin_0
  N3: M1.6, microSD_Transflash1.DI, R3.Pin_0
  N4: M1.GND-15, M1.GND-27, microSD_Transflash1.GND
  N5: M1.3V3-17, M1.3V3-18, R1.Pin_1, R2.Pin_1, R3.Pin_1, R4.Pin_1
  N6: M1.1, microSD_Transflash1.CS, R4.Pin_0
  N7: M1.5V-28, M1.5V-29, microSD_Transflash1.VCC

notes:
  GPIO1 -> CS
  GPIO4 -> MOSI
  GPIO5 -> CLK
  GPIO6 -> MISO
  Sdcard VCC -> 5V

custom parts:
  ESP32-C3-DevKitM-1: Espressif Esp32 DevKit v1 is one of the development board created by DOIT to evaluate the ESP-WROOM-32 module. It is based on the ESP32 microcontroller that boasts Wifi, Bluetooth, Ethernet and Low Power support all in a single chip. (vanepp) Feb 2021: converted to ESP32-C3-DevKitM-1. This chip is 30pins long (2 x15) and 11 pins width.
