# Fritzing sketch audio_player_ex (saved by Fritzing 0.9.6b)
breadboards: 1

parts:
  J3 = shrouded pin header, 24 pins [form="♂ (shrouded male)"]
  S4 = Pushbutton [package="[THT]"]
  S5 = Pushbutton [package="[THT]"]
  S6 = Pushbutton [package="[THT]"]
  R4 = Resistor [tolerance=±5% resistance=10k package="2512 [SMD]"]
  R5 = Resistor [tolerance=±5% resistance=10k package="2512 [SMD]"]
  R6 = Resistor [tolerance=±5% resistance=10k package="2512 [SMD]"]

nets:
  N1: J3.pin13, R4.Pin_1, R5.Pin_1, R6.Pin_1
  N2: J3.pin14, J3.pin15, S4.Pin_3, S4.Pin_4, S5.Pin_3, S5.Pin_4, S6.Pin_3, S6.Pin_4
  N3: J3.pin19, S6.Pin_1, S6.Pin_2, R6.Pin_0
  N4: J3.pin20, S5.Pin_1, S5.Pin_2, R5.Pin_0
  N5: J3.pin21, J3.pin22, S4.Pin_1, S4.Pin_2, R4.Pin_0

notes:
  ESP32-S3-BOX3-BREAD
  Gnd -> black
  3V3 -> red
  GPIO12 -> yellow
  GPIO11 -> Green
  GPIO14 -> Blue
