# Fritzing sketch rmaker_mqtt_ex (saved by Fritzing 0.9.6b)

parts:
  R1 = Photocell (LDR) [package=THT]
  R2 = Resistor [tolerance=±5% resistance=10000 package="0402 [SMD]"]
  M1 = ESP32-C3-DevKitM-1 [part_number=ESP32-C3-DevKitM-1]

nets:
  N1: R1.pin_1, M1.GND-1, M1.GND-12
  N2: R2.Pin_0, M1.4
  N3: R2.Pin_1, M1.3V3-17

notes:
  Devkit pins:
  GND
  3V3
  GPIO 4

custom parts:
  ESP32-C3-DevKitM-1: Espressif Esp32 DevKit v1 is one of the development board created by DOIT to evaluate the ESP-WROOM-32 module. It is based on the ESP32 microcontroller that boasts Wifi, Bluetooth, Ethernet and Low Power support all in a single chip. (vanepp) Feb 2021: converted to ESP32-C3-DevKitM-1. This chip is 30pins long (2 x15) and 11 pins width.
